# Fritzing sketch LPOS-enhed (saved by Fritzing 0.9.6b)
breadboards: 1

parts:
  Mod1 = Arduino MKR Wifi 1010
  M1 = Heart Rate Sensor
  S2 = Pushbutton [package="[THT]"]

nets:
  GND: Mod1.GND, M1.GND, S2.Pin_3, S2.Pin_4
  N1: Mod1.A1, M1.SIG
  N2: Mod1.D7, S2.Pin_1, S2.Pin_2
  +5V: Mod1.+5V, M1.VCC

notes:
  Changed to "A" for analog.

custom parts:
  Arduino MKR Wifi 1010: Arduino MKR Wifi 1010, SAMD21 Cortex-M0+ 32bit Low Power ARM MCU,Flash Memory 256 KB, SRAM 32KB, 48mhz clock, Ublok Wifi interface.
  Heart Rate Sensor: The DFRobot heart rate sensor is a thumb-sized heart rate monitor designed for Arduino microcontrollers. It includes a Gravity interface, for easy plug-and-play connectivity. This sensor is a pulse sensor which is developed based on PPG (PhotoPlethysmoGraphy) techniques. This is a simple and low-cost optical technique that can be used to detect blood volume changes in the microvascular bed of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
